// Logisim project COMBINATIONALDIVIDER.circ as structural Verilog: 1 circuit, main circuit main
module main (
);

  wire and_1_out, and_2_out, and_3_out, and_4_out, and_5_out, and_6_out, and_7_out, and_8_out, and_9_out,
       and_10_out, and_11_out, and_12_out, and_13_out, and_14_out, and_15_out, and_16_out, and_17_out,
       and_18_out, and_19_out, and_20_out, and_21_out, and_22_out, and_23_out, and_24_out, and_25_out,
       and_26_out, and_27_out, and_28_out, dipswitch_1_p1, dipswitch_2_p1, dipswitch_2_p2, dipswitch_2_p3,
       dipswitch_2_p4, not_1_out, not_2_out, not_3_out, not_4_out, not_5_out, not_6_out, not_7_out,
       not_8_out, not_9_out, not_10_out, not_11_out, not_12_out, not_13_out, not_14_out, or_1_out, or_2_out,
       or_4_out, or_5_out, or_6_out, or_7_out, or_8_out, or_9_out, or_10_out, or_11_out, or_12_out,
       or_14_out, undriven, undriven_2, undriven_3, xor_1_out, xor_2_out, xor_3_out, xor_4_out, xor_5_out,
       xor_6_out, xor_7_out, xor_8_out, xor_9_out, xor_10_out, xor_11_out, xor_12_out, xor_13_out, xor_14_out;

  // DipSwitch #(.number(4)) dipswitch_1: pin names not known; wires that end beside it: dipswitch_1_p1
  // DipSwitch #(.number(3)) dipswitch_2: pin names not known; wires that end beside it: dipswitch_2_p1, dipswitch_2_p2, dipswitch_2_p3, dipswitch_2_p4
  not not_1 (not_1_out, dipswitch_2_p2);
  // NOT_Gate not_2 has open pins: in=open, out=not_2_out
  not not_3 (not_3_out, dipswitch_2_p2);
  xor xor_1 (xor_1_out, dipswitch_2_p1, not_1_out);
  and and_1 (and_1_out, dipswitch_2_p1, not_1_out);
  xor xor_2 (xor_2_out, dipswitch_1_p1, not_3_out);
  and and_2 (and_2_out, dipswitch_1_p1, not_3_out);
  xor xor_3 (xor_3_out, undriven, not_2_out);
  and and_3 (and_3_out, undriven, not_2_out);
  xor xor_4 (xor_4_out, xor_1_out, 1'b1);
  and and_4 (and_4_out, xor_1_out, 1'b1);
  not not_4 (not_4_out, or_11_out);
  xor xor_5 (xor_5_out, xor_2_out, 1'b1);
  and and_5 (and_5_out, xor_2_out, 1'b1);
  xor xor_6 (xor_6_out, xor_3_out, 1'b1);
  and and_6 (and_6_out, xor_3_out, 1'b1);
  or or_1 (or_1_out, and_4_out, and_1_out);
  and and_7 (and_7_out, dipswitch_2_p1, not_4_out);
  and and_8 (and_8_out, xor_4_out, or_11_out);
  not not_5 (not_5_out, or_12_out);
  not not_6 (not_6_out, undriven_2);
  or or_2 (or_2_out, and_5_out, and_2_out);
  and and_9 (and_9_out, dipswitch_1_p1, not_5_out);
  and and_10 (and_10_out, xor_5_out, or_12_out);
  // OR_Gate or_3 has open pins: in0=and_6_out, in1=and_3_out, out=open
  and and_11 (and_11_out, undriven_3, not_6_out);
  and and_12 (and_12_out, xor_6_out, undriven_2);
  not not_7 (not_7_out, dipswitch_2_p3);
  or or_4 (or_4_out, and_7_out, and_8_out);
  not not_8 (not_8_out, dipswitch_2_p3);
  or or_5 (or_5_out, and_9_out, and_10_out);
  or or_6 (or_6_out, and_11_out, and_12_out);
  xor xor_7 (xor_7_out, 1'b0, not_7_out);
  and and_13 (and_13_out, 1'b0, not_7_out);
  xor xor_8 (xor_8_out, xor_7_out, or_1_out);
  and and_14 (and_14_out, xor_7_out, or_1_out);
  xor xor_9 (xor_9_out, or_4_out, not_8_out);
  and and_15 (and_15_out, or_4_out, not_8_out);
  not not_9 (not_9_out, or_11_out);
  and and_16 (and_16_out, xor_9_out, or_2_out);
  or or_7 (or_7_out, and_14_out, and_13_out);
  and and_17 (and_17_out, 1'b0, not_9_out);
  and and_18 (and_18_out, xor_8_out, or_11_out);
  xor xor_10 (xor_10_out, xor_9_out, or_2_out);
  or or_8 (or_8_out, and_16_out, and_15_out);
  not not_10 (not_10_out, or_12_out);
  or or_9 (or_9_out, and_17_out, and_18_out);
  and and_19 (and_19_out, or_4_out, not_10_out);
  and and_20 (and_20_out, xor_10_out, or_12_out);
  not not_11 (not_11_out, dipswitch_2_p4);
  not not_12 (not_12_out, dipswitch_2_p4);
  or or_10 (or_10_out, and_19_out, and_20_out);
  xor xor_11 (xor_11_out, 1'b0, not_11_out);
  and and_21 (and_21_out, 1'b0, not_11_out);
  xor xor_12 (xor_12_out, or_9_out, not_12_out);
  and and_22 (and_22_out, or_9_out, not_12_out);
  xor xor_13 (xor_13_out, xor_11_out, or_7_out);
  and and_23 (and_23_out, xor_11_out, or_7_out);
  not not_13 (not_13_out, or_11_out);
  xor xor_14 (xor_14_out, xor_12_out, or_8_out);
  and and_24 (and_24_out, xor_12_out, or_8_out);
  or or_11 (or_11_out, and_23_out, and_21_out);
  and and_25 (and_25_out, 1'b0, not_13_out);
  and and_26 (and_26_out, xor_13_out, or_11_out);
  not not_14 (not_14_out, or_12_out);
  or or_12 (or_12_out, and_24_out, and_22_out);
  and and_27 (and_27_out, or_9_out, not_14_out);
  and and_28 (and_28_out, xor_14_out, or_12_out);
  // OR_Gate or_13 has open pins: in0=and_25_out, in1=and_26_out, out=open
  LED led_1 (.in(or_11_out));
  or or_14 (or_14_out, and_27_out, and_28_out);
  LED led_2 (.in(or_12_out));

  // Notes on the sheet:
  //   D2
  //   D3
  //   d0
  //   FA (2's complement)
  //   FA (2's complement)
  //   FA (2's complement)
  //   Signal line (Quotient)
  //   Signal line (Quotient)
  //   Signal line (Quotient)
  //   Sum
  //   Cout
  //   Mux
  //   Sum
  //   Sum
  //   Cout
  //   Mux
  //   Cout
  //   Mux
  //   Sum
  //   FA (2's complement)
  //   Signal line (Quotient)
  //   Sum
  //   Signal line (Quotient)
  //   Cout
  //   Mux
  //   Sum
  //   Cout
  //   Mux
  //   Sum
  //   FA (2's complement)
  //   Signal line (Quotient)
  //   Sum
  //   Cout
  //   Mux
  //   Sum
  //   Cout
  //   Mux
endmodule
